// Logisim project Oefening5.circ as structural Verilog: 1 circuit, main circuit main
module main (
  input  in_1,
  input  in_2,
  input  in_3,
  output MIDDEN,
  output LINKSBOVEN,
  output BOVEN,
  output RECHTSBOVEN,
  output RECHTSBENEDEN,
  output BENEDEN,
  output LINKSBENEDEN
);

  wire and_1_out, and_2_out, and_3_out, and_4_out, and_5_out, and_6_out, and_7_out, and_8_out, not_1_out,
       not_2_out, not_3_out;

  not not_1 (not_1_out, in_1);
  not not_2 (not_2_out, in_2);
  not not_3 (not_3_out, in_3);
  and and_1 (and_1_out, not_1_out, not_2_out, not_3_out);
  and and_2 (and_2_out, in_3, not_2_out, not_1_out);
  and and_3 (and_3_out, not_3_out, in_2, not_1_out);
  and and_4 (and_4_out, in_3, in_2, not_1_out);
  and and_5 (and_5_out, not_3_out, not_2_out, in_1);
  and and_6 (and_6_out, in_3, not_2_out, in_1);
  and and_7 (and_7_out, not_3_out, in_2, in_1);
  and and_8 (and_8_out, in_3, in_2, in_1);
  or or_1 (MIDDEN, and_3_out, and_4_out, and_5_out, and_6_out, and_7_out);
  or or_2 (LINKSBOVEN, and_1_out, and_5_out, and_6_out, and_7_out);
  or or_3 (BOVEN, and_1_out, and_3_out, and_4_out, and_6_out, and_7_out, and_8_out);
  or or_4 (RECHTSBOVEN, and_4_out, and_1_out, and_2_out, and_3_out, and_5_out, and_8_out);
  or or_5 (RECHTSBENEDEN, and_1_out, and_2_out, and_4_out, and_5_out, and_6_out, and_7_out, and_8_out);
  or or_6 (BENEDEN, and_1_out, and_3_out, and_4_out, and_6_out, and_7_out);
  or or_7 (LINKSBENEDEN, and_1_out, and_3_out, and_7_out);
  _7_Segment_Display u_7_segment_display_1 (
    .g(MIDDEN), .f(LINKSBOVEN), .a(BOVEN), .b(RECHTSBOVEN), .e(LINKSBENEDEN), .d(BENEDEN), .c(RECHTSBENEDEN));  // open: dp

  // Notes on the sheet:
  //   Voor 0
  //   Voor 1
  //   Voor 2
  //   Voor 3
  //   Voor 4
  //   Voor 5
  //   Voor 6
  //   Voor 7
endmodule
