// Logisim project Oefening1.circ as structural Verilog: 1 circuit, main circuit 1b-adder
module _1b_adder (
  input  a,
  input  b,
  input  C_in,
  output s,
  output C_out
);

  wire and_1_out, and_2_out, xor_1_out;

  xor xor_1 (xor_1_out, a, b);
  and and_1 (and_1_out, xor_1_out, C_in);
  and and_2 (and_2_out, a, b);
  xor xor_2 (s, xor_1_out, C_in);
  or or_1 (C_out, and_1_out, and_2_out);
endmodule
