// Logisim project 12bitsCLA.circ as structural Verilog: 3 circuits, main circuit 12bCLA
// 1b adder
module _1b_adder (
  input  a,
  input  b,
  input  C_in,
  output s,
  output C_out
);

  wire and_1_out, and_2_out, xor_1_out;

  xor xor_1 (xor_1_out, a, b);
  and and_1 (and_1_out, xor_1_out, C_in);
  and and_2 (and_2_out, a, b);
  xor xor_2 (s, xor_1_out, C_in);
  or or_1 (C_out, and_1_out, and_2_out);
endmodule

module _12bCLA (
  input  C_0,
  input  [11:0] a,
  input  [11:0] b,
  output [11:0] out_4,
  output Overflow
);

  wire and_1_out, and_2_out, and_3_out, and_4_out, and_5_out, and_6_out, n4bcla_1_g, n4bcla_1_p, n4bcla_2_g,
       n4bcla_2_p, n4bcla_3_g, n4bcla_3_p, nor_1_out, or_1_out, or_2_out, or_3_out, or_4_out;

  _4bCLA u_4bcla_1 (
    .a(a[11:8]), .c_0(or_2_out), .b(b[11:8]), .a_b(out_4[11:8]), .P(n4bcla_1_p), .G(n4bcla_1_g));  // open: out_4
  _4bCLA u_4bcla_2 (
    .a(a[3:0]), .c_0(C_0), .b(b[3:0]), .a_b(out_4[3:0]), .P(n4bcla_2_p), .G(n4bcla_2_g));  // open: out_4
  _4bCLA u_4bcla_3 (
    .a(a[7:4]), .c_0(or_1_out), .b(b[7:4]), .a_b(out_4[7:4]), .P(n4bcla_3_p), .G(n4bcla_3_g));  // open: out_4
  and and_1 (and_1_out, n4bcla_2_p, C_0);
  or or_1 (or_1_out, and_1_out, n4bcla_2_g);
  and and_2 (and_2_out, n4bcla_3_p, n4bcla_2_p, C_0);
  and and_3 (and_3_out, n4bcla_3_p, n4bcla_2_g);
  or or_2 (or_2_out, and_3_out, n4bcla_3_g, and_2_out);
  nor nor_1 (nor_1_out, a[11], b[11]);
  and and_4 (and_4_out, a[11], b[11]);
  and and_5 (and_5_out, ~b[11], out_4[11]);  // AND_Gate
  and and_6 (and_6_out, b[11], ~out_4[11]);  // AND_Gate
  or or_3 (or_3_out, nor_1_out, and_4_out);
  or or_4 (or_4_out, and_5_out, and_6_out);
  and and_7 (Overflow, or_3_out, or_4_out);

  // Notes on the sheet:
  //   G boven, P onder
endmodule

// 4b CLA
module _4bCLA (
  input  [3:0] a,
  input  c_0,
  input  [3:0] b,
  output out_4,
  output P,
  output [3:0] a_b,
  output G
);

  wire and_1_out, and_2_out, and_3_out, and_4_out, and_5_out, and_6_out, and_7_out, and_8_out, and_9_out,
       c_1_out, c_3_out, g_0_out, g_1_out, g_2_out, g_3_out, p_0_out, p_1_out, p_2_out, p_3_out;

  _1b_adder u_1b_adder_1 (.a(a[3]), .b(b[3]), .C_in(c_3_out), .s(a_b[3]));  // open: C_out
  _1b_adder u_1b_adder_2 (.a(a[2]), .b(b[2]), .C_in(out_4), .s(a_b[2]));  // open: C_out
  and g_3 (g_3_out, a[3], b[3]);
  or p_3 (p_3_out, a[3], b[3]);
  and g_2 (g_2_out, a[2], b[2]);
  or p_2 (p_2_out, a[2], b[2]);
  and g_1 (g_1_out, a[1], b[1]);
  or p_1 (p_1_out, a[1], b[1]);
  and g_0 (g_0_out, a[0], b[0]);
  or p_0 (p_0_out, a[0], b[0]);
  _1b_adder u_1b_adder_3 (.a(a[0]), .b(b[0]), .C_in(c_0), .s(a_b[0]));  // open: C_out
  and and_1 (and_1_out, p_0_out, c_0);
  _1b_adder u_1b_adder_4 (.a(a[1]), .b(b[1]), .C_in(c_1_out), .s(a_b[1]));  // open: C_out
  or c_1 (c_1_out, g_0_out, and_1_out);
  and and_2 (and_2_out, p_1_out, g_0_out);
  or c_2 (out_4, g_1_out, and_2_out, and_3_out);
  and and_3 (and_3_out, p_1_out, p_0_out, c_0);
  and and_4 (and_4_out, p_2_out, g_1_out);
  or c_3 (c_3_out, g_2_out, and_4_out, and_5_out, and_6_out);
  and and_5 (and_5_out, p_2_out, p_1_out, g_0_out);
  and and_6 (and_6_out, p_2_out, p_1_out, p_0_out, c_0);
  and u_P (P, p_0_out, p_1_out, p_2_out, p_3_out);
  and and_7 (and_7_out, p_3_out, p_2_out, g_1_out);
  and and_8 (and_8_out, p_3_out, g_2_out);
  or u_G (G, g_3_out, and_8_out, and_7_out, and_9_out);
  and and_9 (and_9_out, p_3_out, p_2_out, p_1_out, g_0_out);
endmodule
