// Logisim project ALU_Group10_12.circ as structural Verilog: 4 circuits, main circuit main
module main (
  output halt,
  output [12:0] counter,
  output [3:0] op,
  output [11:0] a,
  output [11:0] b,
  output [11:0] oracle,
  output [11:0] result,
  output err_oracle,
  output error,
  output ok,
  output start_delimiter
);

  wire and_1_out, and_2_out, clock_1_out, comparator_1_eq, comparator_2_eq;

  Clock clock_1 (.out(clock_1_out));
  Counter #(.width(13), .max('h1fff), .trigger("falling")) counter_1 (
    .Q(counter), .carry(halt), .clk(clock_1_out));  // open: load, D, count, clr
  RAM #(.addrWidth(16), .dataWidth(4), .bus("separate")) ram_1 (
    .addr({counter, 3'b000}), .data(op), .ld(1'b1));  // open: din, str, sel, clk, clr
  RAM #(.addrWidth(16), .dataWidth(12), .bus("separate")) ram_2 (
    .addr({counter, 3'b001}), .data(a), .ld(1'b1));  // open: din, str, sel, clk, clr
  RAM #(.addrWidth(16), .dataWidth(12), .bus("separate")) ram_3 (
    .addr({counter, 3'b010}), .data(b), .ld(1'b1));  // open: din, str, sel, clk, clr
  RAM #(.addrWidth(16), .dataWidth(12), .bus("separate")) ram_4 (
    .addr({counter, 3'b011}), .data(oracle), .ld(1'b1));  // open: din, str, sel, clk, clr
  RAM #(.addrWidth(16), .dataWidth(1), .bus("separate")) ram_5 (
    .addr({counter, 3'b100}), .data(err_oracle), .ld(1'b1));  // open: din, str, sel, clk, clr
  RAM #(.addrWidth(16), .dataWidth(1), .bus("separate")) ram_6 (
    .addr({counter, 3'b101}), .data(start_delimiter), .ld(1'b1));  // open: din, str, sel, clk, clr
  _12_bit_ALU u_12_bit_alu_1 (.ALU_code(op), .a(a), .b(b), .overflow(error), .result(result));
  Comparator #(.width(1), .mode("unsigned")) comparator_1 (
    .a(error), .b(err_oracle), .eq(comparator_1_eq));  // open: gt, lt
  Comparator #(.width(12)) comparator_2 (.a(result), .b(oracle), .eq(comparator_2_eq));  // open: gt, lt
  and and_1 (and_1_out, comparator_1_eq, error);
  and and_2 (and_2_out, comparator_2_eq, comparator_1_eq, ~error);  // AND_Gate
  or or_1 (ok, and_1_out, and_2_out);

  // Notes on the sheet:
  //   You must complete the circuit '12-bit ALU' instead, ALU van Wasim en Mathijs
  //   DO NOT EDIT THIS CIRCUIT!
endmodule

module _12_bit_ALU (
  input  [3:0] ALU_code,
  input  [11:0] a,
  input  [11:0] b,
  output [11:0] result,
  output overflow
);

  wire n12bcla_1_overflow, n12bcla_2_overflow, n12bcla_3_overflow, n12bcla_4_overflow, Sub_out, xor_1_out;
  wire [11:0] and_1_out, gt_lt_1_gt, gt_lt_1_lt, n12bcla_1_out_4, n12bcla_2_out_4, n12bcla_3_out_4,
       n12bcla_4_out_4, neq_eq_1_eq, neq_eq_1_neq, not_1_out, not_2_out, or_1_out;

  _12bCLA u_12bcla_1 (.C_0(1'b0), .a(a), .b(b), .Overflow(n12bcla_1_overflow), .out_4(n12bcla_1_out_4));
  _12bCLA u_12bcla_2 (.C_0(1'b0), .a(not_1_out), .b(12'h1), .Overflow(n12bcla_2_overflow), .out_4(n12bcla_2_out_4));
  assign not_1_out = ~b;  // NOT_Gate not_1, 12 bits wide
  _12bCLA u_12bcla_3 (.C_0(1'b0), .a(a), .b(n12bcla_2_out_4), .Overflow(n12bcla_3_overflow), .out_4(n12bcla_3_out_4));
  xor Sub (Sub_out, n12bcla_2_overflow, n12bcla_3_overflow);
  assign and_1_out = a & b;  // AND_Gate and_1, 12 bits wide
  assign or_1_out = a | b;  // OR_Gate or_1, 12 bits wide
  gt_lt gt_lt_1 (.A(a), .B(b), .gt(gt_lt_1_gt), .lt(gt_lt_1_lt));
  xor xor_1 (xor_1_out, a[11], a[10]);
  neq_eq neq_eq_1 (.in_1(b), .in_2(a), .eq(neq_eq_1_eq), .neq(neq_eq_1_neq));  // open: bitwise_eq
  assign not_2_out = ~a;  // NOT_Gate not_2, 12 bits wide
  _12bCLA u_12bcla_4 (.C_0(1'b0), .a(not_2_out), .b(12'h1), .Overflow(n12bcla_4_overflow), .out_4(n12bcla_4_out_4));
  Multiplexer #(.select(4), .width(12), .enable("false")) multiplexer_1 (
    .in0(n12bcla_1_out_4), .in1(n12bcla_3_out_4), .in2(and_1_out), .in3(or_1_out), .in4(gt_lt_1_lt),
    .in5(gt_lt_1_gt), .in6(neq_eq_1_eq), .in7(neq_eq_1_neq), .in8(not_2_out), .in9(n12bcla_4_out_4),
    .in10({a[10:0], 1'b0}), .in11({1'b0, a[11:1]}), .in12({a[10:0], 1'b0}), .in13({{2{a[11]}}, a[10:1]}),
    .in14({12{1'b0}}), .in15(a), .out(result), .sel(ALU_code));
  Multiplexer #(.select(4), .enable("false")) multiplexer_2 (
    .in0(n12bcla_1_overflow), .in1(Sub_out), .in2(1'b0), .in3(1'b0), .in4(1'b0), .in5(1'b0), .in6(1'b0),
    .in7(1'b0), .in8(1'b0), .in9(n12bcla_4_overflow), .in10(1'b0), .in11(1'b0), .in12(xor_1_out),
    .in13(1'b0), .in14(1'b0), .in15(1'b0), .out(overflow), .sel(ALU_code));

  // Notes on the sheet:
  //   This circuit is used as a block in the main circuit, and its layout must remain unchanged. The circuit called "main" should be the main circuit of this file.
  //   0000: ADD - OK
  //   0001: SUBTRACT - OK
  //   0010: AND - OK
  //   0011: OR - OK
  //   0100: LESS THAN - OK
  //   0110: EQUALS - OK
  //   1000: NOT A - OK
  //   1001: INV A - OK
  //   1010: SLL A - OK
  //   1011: SRL A - OK
  //   1100: SLA A - OK
  //   1101: SRA A - OK
  //   1110: GEN 0 - OK
  //   ALU Codes refrence guide:
  //   0101: GREATER THAN - OK
  //   0111: DOESN'T EQUAL - OK
  //   1111: PASSTHROUGH A - OK
  //   Do not change the circuit appearance.
  //   Add
  //   Passthrough
  //   Sub
  //   DO NOT CHANGE THE INPUTS AND OUTPUTS OF THIS CIRCUIT!
  //   Sub
  //   Do not add/remove inputs or outputs. Do not even change their location or orientation.
  //   And
  //   Or
  //   Sll-sla
  //   Sla
  //   Srl
  //   Sra
  //   Not
  //   Inv
  //   Gen 0
endmodule

module neq_eq (
  input  [11:0] in_1,
  input  [11:0] in_2,
  output [11:0] eq,
  output [11:0] neq,
  output [11:0] bitwise_eq
);

  wire [11:0] and_1_out, and_2_out, not_1_out, not_2_out;

  assign and_1_out = in_1 & in_2;  // AND_Gate and_1, 12 bits wide
  assign not_1_out = ~in_1;  // NOT_Gate not_1, 12 bits wide
  assign not_2_out = ~in_2;  // NOT_Gate not_2, 12 bits wide
  assign and_2_out = not_2_out & not_1_out;  // AND_Gate and_2, 12 bits wide
  assign bitwise_eq = and_1_out | and_2_out;  // OR_Gate or_1, 12 bits wide
  and and_3 (eq[0], bitwise_eq[0], bitwise_eq[1], bitwise_eq[2], bitwise_eq[3], bitwise_eq[4], bitwise_eq[5], bitwise_eq[6], bitwise_eq[7], bitwise_eq[8], bitwise_eq[9], bitwise_eq[10], bitwise_eq[11]);
  not not_3 (neq[0], eq[0]);

  assign eq[11:1] = {11{1'b0}};
  assign neq[11:1] = {11{1'b0}};
endmodule

module gt_lt (
  input  [11:0] A,
  input  [11:0] B,
  output [11:0] gt,
  output [11:0] lt
);

  wire n12bcla_1_overflow, n12bcla_2_overflow, not_2_out, not_3_out, xor_1_out;
  wire [11:0] n12bcla_1_out_4, n12bcla_2_out_4, neq_eq_1_neq, not_1_out;

  assign not_1_out = ~B;  // NOT_Gate not_1, 12 bits wide
  _12bCLA u_12bcla_1 (.C_0(1'b0), .a(not_1_out), .b(12'h1), .Overflow(n12bcla_1_overflow), .out_4(n12bcla_1_out_4));
  _12bCLA u_12bcla_2 (.C_0(1'b0), .a(A), .b(n12bcla_1_out_4), .Overflow(n12bcla_2_overflow), .out_4(n12bcla_2_out_4));
  xor xor_1 (xor_1_out, n12bcla_2_overflow, n12bcla_1_overflow);
  neq_eq neq_eq_1 (.in_1(A), .in_2(B), .neq(neq_eq_1_neq));  // open: eq, bitwise_eq
  not not_2 (not_2_out, n12bcla_2_out_4[11]);
  not not_3 (not_3_out, lt[0]);
  Multiplexer #(.enable("false")) multiplexer_1 (
    .in0(n12bcla_2_out_4[11]), .in1(not_2_out), .out(lt[0]), .sel(xor_1_out));
  and and_1 (gt[0], neq_eq_1_neq[0], not_3_out);

  assign gt[11:1] = {11{1'b0}};
  assign lt[11:1] = {11{1'b0}};

  // Notes on the sheet:
  //   Sub
  //   Sub
endmodule
