// Logisim project CA-4.circ as structural Verilog: 6 circuits, main circuit register
module register (
  input  [11:0] D,
  input  reset,
  input  write,
  input  C,
  output [11:0] Q
);

  wire undriven, undriven_2, undriven_3, undriven_4, undriven_5, undriven_6, undriven_7, undriven_8,
       undriven_9, undriven_10, undriven_11;

  D_Flip_Flop #(.trigger("falling")) d_ff_1 (
    .clk(C), .D(D[0]), .Q(Q[0]), .preset(undriven), .en(write), .reset(reset));  // open: Qn
  D_Flip_Flop #(.trigger("falling")) d_ff_2 (
    .clk(C), .D(D[1]), .Q(Q[1]), .preset(undriven_2), .en(write), .reset(reset));  // open: Qn
  D_Flip_Flop #(.trigger("falling")) d_ff_3 (
    .clk(C), .D(D[2]), .Q(Q[2]), .preset(undriven_3), .en(write), .reset(reset));  // open: Qn
  D_Flip_Flop #(.trigger("falling")) d_ff_4 (
    .clk(C), .D(D[3]), .Q(Q[3]), .preset(undriven_4), .en(write), .reset(reset));  // open: Qn
  D_Flip_Flop #(.trigger("falling")) d_ff_5 (
    .clk(C), .D(D[4]), .Q(Q[4]), .preset(undriven_5), .en(write), .reset(reset));  // open: Qn
  D_Flip_Flop #(.trigger("falling")) d_ff_6 (
    .clk(C), .D(D[5]), .Q(Q[5]), .preset(undriven_6), .en(write), .reset(reset));  // open: Qn
  D_Flip_Flop #(.trigger("falling")) d_ff_7 (
    .clk(C), .D(D[6]), .Q(Q[6]), .en(write), .reset(reset));  // open: Qn, preset
  D_Flip_Flop #(.trigger("falling")) d_ff_8 (
    .clk(C), .D(D[7]), .Q(Q[7]), .preset(undriven_7), .en(write), .reset(reset));  // open: Qn
  D_Flip_Flop #(.trigger("falling")) d_ff_9 (
    .clk(C), .D(D[8]), .Q(Q[8]), .preset(undriven_8), .en(write), .reset(reset));  // open: Qn
  D_Flip_Flop #(.trigger("falling")) d_ff_10 (
    .clk(C), .D(D[9]), .Q(Q[9]), .preset(undriven_9), .en(write), .reset(reset));  // open: Qn
  D_Flip_Flop #(.trigger("falling")) d_ff_11 (
    .clk(C), .D(D[10]), .Q(Q[10]), .preset(undriven_10), .en(write), .reset(reset));  // open: Qn
  D_Flip_Flop #(.trigger("falling")) d_ff_12 (
    .clk(C), .D(D[11]), .Q(Q[11]), .preset(undriven_11), .en(write), .reset(reset));  // open: Qn
endmodule

module registerfile (
  input  C,
  input  reset,
  input  [2:0] rs,
  input  [2:0] rt,
  input  [2:0] rd,
  input  [11:0] Data,
  input  write,
  output [11:0] S,
  output [11:0] T
);

  wire demultiplexer_1_out0, demultiplexer_1_out1, demultiplexer_1_out2, demultiplexer_1_out3,
       demultiplexer_1_out4, demultiplexer_1_out5, demultiplexer_1_out6, demultiplexer_1_out7;
  wire [11:0] register_1_q, register_2_q, register_3_q, register_4_q, register_5_q, register_6_q,
       register_7_q;

  Demultiplexer #(.select(3), .disabled(0), .enable("false")) demultiplexer_1 (
    .out0(demultiplexer_1_out0), .out1(demultiplexer_1_out1), .out2(demultiplexer_1_out2),
    .out3(demultiplexer_1_out3), .out4(demultiplexer_1_out4), .out5(demultiplexer_1_out5),
    .out6(demultiplexer_1_out6), .out7(demultiplexer_1_out7), .in(write), .sel(rd));
  register register_1 (.D(Data), .Q(register_1_q), .reset(reset), .write(demultiplexer_1_out1), .C(C));
  register register_2 (.D(Data), .Q(register_2_q), .reset(reset), .write(demultiplexer_1_out2), .C(C));
  register register_3 (.D(Data), .Q(register_3_q), .reset(reset), .write(demultiplexer_1_out3), .C(C));
  register register_4 (.D(Data), .Q(register_4_q), .reset(reset), .write(demultiplexer_1_out4), .C(C));
  register register_5 (.D(Data), .Q(register_5_q), .reset(reset), .write(demultiplexer_1_out5), .C(C));
  register register_6 (.D(Data), .Q(register_6_q), .reset(reset), .write(demultiplexer_1_out6), .C(C));
  register register_7 (.D(Data), .Q(register_7_q), .reset(reset), .write(demultiplexer_1_out7), .C(C));
  Multiplexer #(.select(3), .width(12), .enable("false")) multiplexer_1 (
    .in0({12{1'b0}}), .in1(register_1_q), .in2(register_2_q), .in3(register_3_q), .in4(register_4_q),
    .in5(register_5_q), .in6(register_6_q), .in7(register_7_q), .out(S), .sel(rs));
  Multiplexer #(.select(3), .width(12), .enable("false")) multiplexer_2 (
    .in0({12{1'b0}}), .in1(register_1_q), .in2(register_2_q), .in3(register_3_q), .in4(register_4_q),
    .in5(register_5_q), .in6(register_6_q), .in7(register_7_q), .out(T), .sel(rt));
endmodule

module counter (
  input  Force_Reset,
  input  [11:0] D,
  input  C,
  output [11:0] \output 
);

  wire comparator_1_eq, or_1_out;
  wire [11:0] n12bcla_1_out_4;

  _12bCLA u_12bcla_1 (.C_0(1'b0), .a(\output ), .b(12'h1), .out_4(n12bcla_1_out_4));  // open: Overflow
  Comparator #(.width(12)) comparator_1 (.a(D), .b(\output ), .eq(comparator_1_eq));  // open: gt, lt
  or or_1 (or_1_out, comparator_1_eq, Force_Reset);
  register register_1 (.D(n12bcla_1_out_4), .Q(\output ), .reset(or_1_out), .write(1'b1), .C(C));
endmodule

module counter_with_sub (
  input  Force_Reset,
  input  [11:0] D,
  input  C,
  input  Count_down,
  output [11:0] \output 
);

  wire comparator_1_eq, or_1_out;
  wire [11:0] multiplexer_1_out, n12bcla_1_out_4;

  Multiplexer #(.width(12), .disabled(0), .enable("false")) multiplexer_1 (
    .in0(12'h1), .in1({12{1'b1}}), .out(multiplexer_1_out), .sel(Count_down));
  _12bCLA u_12bcla_1 (.C_0(1'b0), .a(\output ), .b(multiplexer_1_out), .out_4(n12bcla_1_out_4));  // open: Overflow
  Comparator #(.width(12)) comparator_1 (.a(D), .b(\output ), .eq(comparator_1_eq));  // open: gt, lt
  or or_1 (or_1_out, comparator_1_eq, Force_Reset);
  register register_1 (.D(n12bcla_1_out_4), .Q(\output ), .reset(or_1_out), .write(1'b1), .C(C));
endmodule

module finite_state_machine (
);

  wire _1g, _1r, _1y, _2g, _2r, _2y, Clock_out, comparator_1_eq, comparator_1_gt, comparator_2_eq,
       comparator_2_gt, comparator_2_lt, comparator_3_lt, comparator_4_eq, comparator_4_gt, comparator_5_eq,
       comparator_5_gt, comparator_5_lt, comparator_6_lt, or_1_out, or_2_out, or_3_out, or_4_out, or_5_out,
       or_6_out;
  wire [11:0] counter_1_output;

  Clock Clock (.out(Clock_out));
  counter counter_1 (.D(12'h1d), .C(Clock_out), .\output (counter_1_output));  // open: Force_Reset
  // Probe on counter_1_output
  Comparator #(.width(12), .mode("unsigned")) comparator_1 (
    .a(counter_1_output), .b({12{1'b0}}), .gt(comparator_1_gt), .eq(comparator_1_eq));  // open: lt
  Comparator #(.width(12), .mode("unsigned")) comparator_2 (
    .a(counter_1_output), .b(12'h8), .gt(comparator_2_gt), .eq(comparator_2_eq), .lt(comparator_2_lt));
  Comparator #(.width(12), .mode("unsigned")) comparator_3 (
    .a(counter_1_output), .b(12'hc), .lt(comparator_3_lt));  // open: gt, eq
  Comparator #(.width(12), .mode("unsigned")) comparator_4 (
    .a(counter_1_output), .b(12'he), .gt(comparator_4_gt), .eq(comparator_4_eq));  // open: lt
  Comparator #(.width(12), .mode("unsigned")) comparator_5 (
    .a(counter_1_output), .b(12'h16), .gt(comparator_5_gt), .eq(comparator_5_eq), .lt(comparator_5_lt));
  Comparator #(.width(12), .mode("unsigned")) comparator_6 (
    .a(counter_1_output), .b(12'h1a), .lt(comparator_6_lt));  // open: gt, eq
  or or_1 (or_1_out, comparator_1_gt, comparator_1_eq);
  and and_1 (_1g, or_1_out, comparator_2_lt);
  or or_2 (or_2_out, comparator_2_gt, comparator_2_eq);
  and and_2 (_1y, or_2_out, comparator_3_lt);
  or or_3 (or_3_out, comparator_4_gt, comparator_4_eq);
  and and_3 (_2g, or_3_out, comparator_5_lt);
  or or_4 (or_4_out, comparator_5_gt, comparator_5_eq);
  and and_4 (_2y, or_4_out, comparator_6_lt);
  or or_5 (or_5_out, _1g, _1y);
  Multiplexer #(.disabled(0), .enable("false")) multiplexer_1 (.in0(1'b1), .in1(1'b0), .out(_1r), .sel(or_5_out));
  or or_6 (or_6_out, _2g, _2y);
  Multiplexer #(.disabled(0), .enable("false")) multiplexer_2 (.in0(1'b1), .in1(1'b0), .out(_2r), .sel(or_6_out));
  LED led_1 (.in(_1r));
  LED led_2 (.in(_1y));
  LED led_3 (.in(_1g));
  LED led_4 (.in(_2r));
  LED led_5 (.in(_2y));
  LED led_6 (.in(_2g));

  // Notes on the sheet:
  //   Light 1
  //   Light 2
endmodule

module stack (
  input  reset,
  input  Push,
  input  Pop,
  input  [11:0] Data,
  output [11:0] Top_of_Stack,
  output Error
);

  wire and_1_out, and_2_out, and_3_out, C_out, multiplexer_1_out, not_1_out, not_2_out, not_3_out, not_4_out,
       or_1_out, xor_1_out, xor_2_out;
  wire [11:0] multiplexer_2_out, multiplexer_3_out, overflow, ram_1_data, underflow;

  Clock C (.out(C_out));
  not not_1 (not_1_out, multiplexer_1_out);
  Multiplexer #(.enable("false")) multiplexer_1 (.in0(C_out), .out(multiplexer_1_out), .sel(not_2_out));  // open: in1
  not not_2 (not_2_out, xor_1_out);
  not not_3 (not_3_out, Push);
  xor xor_1 (xor_1_out, Push, Pop);
  xor xor_2 (xor_2_out, Push, Pop);
  // Probe on overflow
  counter_with_sub counter_with_sub_1 (
    .D({12{1'b1}}), .C(not_1_out), .\output (overflow), .Force_Reset(reset), .Count_down(Pop));
  _12bCLA u_12bcla_1 (.C_0(1'b0), .a({12{1'b1}}), .b(overflow), .out_4(underflow));  // open: Overflow
  Multiplexer #(.width(12), .enable("false")) multiplexer_2 (
    .in0(overflow), .in1(underflow), .out(multiplexer_2_out), .sel(not_3_out));
  Multiplexer #(.width(12), .enable("false")) multiplexer_3 (
    .in0(Data), .in1({12{1'b0}}), .out(multiplexer_3_out), .sel(Pop));
  RAM #(.addrWidth(12), .dataWidth(12), .bus("separate")) ram_1 (
    .addr(multiplexer_2_out), .din(multiplexer_3_out), .data(ram_1_data), .str(xor_2_out), .sel(not_4_out),
    .clk(C_out), .clr(reset));  // open: ld
  not not_4 (not_4_out, Error);
  and and_1 (and_1_out, not_4_out, xor_1_out);
  and and_2 (and_2_out, overflow[0], overflow[1], overflow[2], overflow[3], overflow[4], overflow[5], overflow[6], overflow[7], overflow[8], overflow[9], overflow[10], overflow[11], Push);
  Multiplexer #(.width(12), .enable("false")) multiplexer_4 (
    .in0(ram_1_data), .in1({12{1'b0}}), .out(Top_of_Stack), .sel(and_1_out));
  S_R_Flip_Flop #(.trigger("falling")) s_r_ff_1 (
    .Q(Error), .preset(or_1_out), .reset(reset));  // open: S, clk, R, Qn, en
  or or_1 (or_1_out, and_2_out, and_3_out);
  and and_3 (and_3_out, Pop, Push);
endmodule
