// Logisim project OurMemory.circ as structural Verilog: 4 circuits, main circuit registerfile
module register (
  input  [11:0] D,
  input  reset,
  input  write,
  input  C,
  output [11:0] Q
);

  wire undriven, undriven_2, undriven_3, undriven_4, undriven_5, undriven_6, undriven_7, undriven_8,
       undriven_9, undriven_10, undriven_11;

  D_Flip_Flop #(.trigger("falling")) d_ff_1 (
    .clk(C), .D(D[0]), .Q(Q[0]), .preset(undriven), .en(write), .reset(reset));  // open: Qn
  D_Flip_Flop #(.trigger("falling")) d_ff_2 (
    .clk(C), .D(D[1]), .Q(Q[1]), .preset(undriven_2), .en(write), .reset(reset));  // open: Qn
  D_Flip_Flop #(.trigger("falling")) d_ff_3 (
    .clk(C), .D(D[2]), .Q(Q[2]), .preset(undriven_3), .en(write), .reset(reset));  // open: Qn
  D_Flip_Flop #(.trigger("falling")) d_ff_4 (
    .clk(C), .D(D[3]), .Q(Q[3]), .preset(undriven_4), .en(write), .reset(reset));  // open: Qn
  D_Flip_Flop #(.trigger("falling")) d_ff_5 (
    .clk(C), .D(D[4]), .Q(Q[4]), .preset(undriven_5), .en(write), .reset(reset));  // open: Qn
  D_Flip_Flop #(.trigger("falling")) d_ff_6 (
    .clk(C), .D(D[5]), .Q(Q[5]), .preset(undriven_6), .en(write), .reset(reset));  // open: Qn
  D_Flip_Flop #(.trigger("falling")) d_ff_7 (
    .clk(C), .D(D[6]), .Q(Q[6]), .en(write), .reset(reset));  // open: Qn, preset
  D_Flip_Flop #(.trigger("falling")) d_ff_8 (
    .clk(C), .D(D[7]), .Q(Q[7]), .preset(undriven_7), .en(write), .reset(reset));  // open: Qn
  D_Flip_Flop #(.trigger("falling")) d_ff_9 (
    .clk(C), .D(D[8]), .Q(Q[8]), .preset(undriven_8), .en(write), .reset(reset));  // open: Qn
  D_Flip_Flop #(.trigger("falling")) d_ff_10 (
    .clk(C), .D(D[9]), .Q(Q[9]), .preset(undriven_9), .en(write), .reset(reset));  // open: Qn
  D_Flip_Flop #(.trigger("falling")) d_ff_11 (
    .clk(C), .D(D[10]), .Q(Q[10]), .preset(undriven_10), .en(write), .reset(reset));  // open: Qn
  D_Flip_Flop #(.trigger("falling")) d_ff_12 (
    .clk(C), .D(D[11]), .Q(Q[11]), .preset(undriven_11), .en(write), .reset(reset));  // open: Qn
endmodule

module registerfile (
  input  C,
  input  reset,
  input  [2:0] rs,
  input  [2:0] rt,
  input  [2:0] rd,
  input  [11:0] Data,
  input  write,
  output [11:0] r0,
  output [11:0] r1,
  output [11:0] r2,
  output [11:0] r3,
  output [11:0] r4,
  output [11:0] r5,
  output [11:0] r6,
  output [11:0] r7,
  output [11:0] S,
  output [11:0] T
);

  wire demultiplexer_1_out0, demultiplexer_1_out1, demultiplexer_1_out2, demultiplexer_1_out3,
       demultiplexer_1_out4, demultiplexer_1_out5, demultiplexer_1_out6, demultiplexer_1_out7;

  Demultiplexer #(.select(3), .disabled(0), .enable("false")) demultiplexer_1 (
    .out0(demultiplexer_1_out0), .out1(demultiplexer_1_out1), .out2(demultiplexer_1_out2),
    .out3(demultiplexer_1_out3), .out4(demultiplexer_1_out4), .out5(demultiplexer_1_out5),
    .out6(demultiplexer_1_out6), .out7(demultiplexer_1_out7), .in(write), .sel(rd));
  register register_1 (.D(Data), .Q(r1), .reset(reset), .write(demultiplexer_1_out1), .C(C));
  register register_2 (.D(Data), .Q(r2), .reset(reset), .write(demultiplexer_1_out2), .C(C));
  register register_3 (.D(Data), .Q(r3), .reset(reset), .write(demultiplexer_1_out3), .C(C));
  register register_4 (.D(Data), .Q(r4), .reset(reset), .write(demultiplexer_1_out4), .C(C));
  register register_5 (.D(Data), .Q(r5), .reset(reset), .write(demultiplexer_1_out5), .C(C));
  register register_6 (.D(Data), .Q(r6), .reset(reset), .write(demultiplexer_1_out6), .C(C));
  register register_7 (.D(Data), .Q(r7), .reset(reset), .write(demultiplexer_1_out7), .C(C));
  Multiplexer #(.select(3), .width(12), .enable("false")) multiplexer_1 (
    .in0({12{1'b0}}), .in1(r1), .in2(r2), .in3(r3), .in4(r4), .in5(r5), .in6(r6), .in7(r7), .out(S), .sel(rs));
  Multiplexer #(.select(3), .width(12), .enable("false")) multiplexer_2 (
    .in0({12{1'b0}}), .in1(r1), .in2(r2), .in3(r3), .in4(r4), .in5(r5), .in6(r6), .in7(r7), .out(T), .sel(rt));

  assign r0 = {12{1'b0}};
endmodule

module counter (
  input  Force_Reset,
  input  [11:0] D,
  input  C,
  output [11:0] \output 
);

  wire comparator_1_eq, or_1_out;
  wire [11:0] n12bcla_1_out_4;

  _12bCLA u_12bcla_1 (.C_0(1'b0), .a(\output ), .b(12'h1), .out_4(n12bcla_1_out_4));  // open: Overflow
  Comparator #(.width(12)) comparator_1 (.a(D), .b(\output ), .eq(comparator_1_eq));  // open: gt, lt
  or or_1 (or_1_out, comparator_1_eq, Force_Reset);
  register register_1 (.D(n12bcla_1_out_4), .Q(\output ), .reset(or_1_out), .write(1'b1), .C(C));
endmodule

module counter_with_sub (
  input  Force_Reset,
  input  [11:0] D,
  input  C,
  input  Count_down,
  output [11:0] \output 
);

  wire comparator_1_eq, or_1_out;
  wire [11:0] multiplexer_1_out, n12bcla_1_out_4;

  Multiplexer #(.width(12), .disabled(0), .enable("false")) multiplexer_1 (
    .in0(12'h1), .in1({12{1'b1}}), .out(multiplexer_1_out), .sel(Count_down));
  _12bCLA u_12bcla_1 (.C_0(1'b0), .a(\output ), .b(multiplexer_1_out), .out_4(n12bcla_1_out_4));  // open: Overflow
  Comparator #(.width(12)) comparator_1 (.a(D), .b(\output ), .eq(comparator_1_eq));  // open: gt, lt
  or or_1 (or_1_out, comparator_1_eq, Force_Reset);
  register register_1 (.D(n12bcla_1_out_4), .Q(\output ), .reset(or_1_out), .write(1'b1), .C(C));
endmodule
