// Logisim project SD_Group10.circ as structural Verilog: 6 circuits, main circuit main
module main (
  output [11:0] pc,
  output [11:0] r0,
  output [11:0] r1,
  output [11:0] r2,
  output [11:0] r3,
  output [11:0] r4,
  output [11:0] r5,
  output [11:0] r6,
  output [11:0] r7,
  output halt
);

  wire and_1_out, clock_1_out, controller_1_alu_immediate, controller_1_load_immediate_register,
       controller_1_read_memory, controller_1_register_write, controller_1_subi, controller_1_use_upper,
       controller_1_write_memory, not_1_out, or_1_out, or_2_out, reset_out;
  wire [2:0] decoder_1_operation_code, decoder_1_rd, decoder_1_rs, decoder_1_rt, multiplexer_4_out;
  wire [3:0] controller_1_alu_operation, decoder_1_operational_function_code;
  wire [11:0] decoder_1_immediate_extended_6_bits, decoder_1_immediate_extended_9_bits, multiplexer_1_out,
       multiplexer_2_out, multiplexer_3_out, multiplexer_5_out, multiplexer_6_out, n12_bit_alu_1_result,
       ram_2_data, registerfile_1_s, registerfile_1_t, shifter_1_out, swap_1_output_1, swap_1_output_2;
  wire [15:0] ram_1_data;

  Halt halt_1 (.instruction(ram_1_data), .clock(clock_1_out), .reset(reset_out), .halt(halt));
  Clock clock_1 (.out(clock_1_out));
  Button reset (.out(reset_out));
  _12BitProgramCounter u_12bitprogramcounter_1 (
    .Branch_relative(1'b0), .Branch_absolute(1'b0), .C(and_1_out), .reset(reset_out), .Instruction_Address(pc));  // open: Branch_value
  and and_1 (and_1_out, ~halt, clock_1_out);  // AND_Gate
  RAM #(.addrWidth(12), .dataWidth(16), .bus("asynch")) ram_1 (.addr(pc), .data(ram_1_data));  // open: sel, ld, clr
  Decoder decoder_1 (
    .Instruction(ram_1_data), .Operation_Code(decoder_1_operation_code), .rd(decoder_1_rd),
    .rs(decoder_1_rs), .rt(decoder_1_rt), .Operational_Function_Code(decoder_1_operational_function_code),
    .Immediate_extended_9_bits(decoder_1_immediate_extended_9_bits),
    .Immediate_extended_6_bits(decoder_1_immediate_extended_6_bits));
  Shifter #(.width(12)) shifter_1 (.in(decoder_1_immediate_extended_9_bits), .\dist (4'b0011), .out(shifter_1_out));
  Multiplexer #(.width(12), .enable("false")) multiplexer_1 (
    .in0(decoder_1_immediate_extended_9_bits), .in1(shifter_1_out), .out(multiplexer_1_out),
    .sel(controller_1_use_upper));
  not not_1 (not_1_out, controller_1_load_immediate_register);
  Multiplexer #(.width(12), .enable("false")) multiplexer_2 (
    .in0(multiplexer_1_out), .in1(n12_bit_alu_1_result), .out(multiplexer_2_out), .sel(not_1_out));
  Controller controller_1 (
    .Operation_code(decoder_1_operation_code),
    .Operational_Function_Code(decoder_1_operational_function_code), .Read_Memory(controller_1_read_memory),
    .Write_Memory(controller_1_write_memory), .SUBI(controller_1_subi),
    .ALU_Operation(controller_1_alu_operation), .Register_Write(controller_1_register_write),
    .Load_Immediate_register(controller_1_load_immediate_register),
    .ALU_Immediate(controller_1_alu_immediate), .Use_Upper(controller_1_use_upper));  // open: Zero_Operation
  Multiplexer #(.width(12), .enable("false")) multiplexer_3 (
    .in0(multiplexer_2_out), .in1(ram_2_data), .out(multiplexer_3_out), .sel(controller_1_read_memory));
  or or_1 (or_1_out, controller_1_write_memory, controller_1_read_memory, controller_1_alu_immediate);
  Multiplexer #(.width(3), .enable("false")) multiplexer_4 (
    .in0(decoder_1_rt), .in1(decoder_1_rd), .out(multiplexer_4_out), .sel(or_1_out));
  registerfile registerfile_1 (
    .C(and_1_out), .reset(reset_out), .rd(decoder_1_rd), .Data(multiplexer_3_out),
    .write(controller_1_register_write), .rs(decoder_1_rs), .rt(multiplexer_4_out), .r0(r0), .r1(r1),
    .r2(r2), .r3(r3), .r4(r4), .r5(r5), .r6(r6), .r7(r7), .S(registerfile_1_s), .T(registerfile_1_t));
  Multiplexer #(.width(12), .enable("false")) multiplexer_5 (
    .in0(registerfile_1_s), .in1(multiplexer_1_out), .out(multiplexer_5_out), .sel(controller_1_alu_immediate));
  or or_2 (or_2_out, controller_1_write_memory, controller_1_read_memory);
  _12_bit_ALU u_12_bit_alu_1 (
    .ALU_code(controller_1_alu_operation), .a(swap_1_output_1), .b(swap_1_output_2),
    .result(n12_bit_alu_1_result));  // open: overflow
  swap swap_1 (
    .Input_1(multiplexer_5_out), .Input_2(multiplexer_6_out), .Output_1(swap_1_output_1),
    .Output_2(swap_1_output_2), .Switch(controller_1_subi));
  Multiplexer #(.width(12), .enable("false")) multiplexer_6 (
    .in0(registerfile_1_t), .in1(decoder_1_immediate_extended_6_bits), .out(multiplexer_6_out), .sel(or_2_out));
  RAM #(.addrWidth(12), .dataWidth(12), .bus("separate")) ram_2 (
    .addr(n12_bit_alu_1_result), .din(registerfile_1_t), .data(ram_2_data), .str(controller_1_write_memory),
    .clk(and_1_out), .ld(controller_1_read_memory));  // open: sel, clr

  // Notes on the sheet:
  //   current instruction
  //   Instruction RAM
  //   clock signal
  //   reset button
  //   reset
  //   DO NOT CHANGE THE INPUTS AND OUTPUTS OF THIS CIRCUIT! Do not add/remove inputs or outputs. Do not even change their location or orientation.
  //   Data RAM
endmodule

module Halt (
  input  [15:0] instruction,
  input  clock,
  input  reset,
  output halt
);

  wire and_1_out, comparator_1_eq, comparator_2_gt, counter_1_carry, or_1_out, or_2_out;
  wire [11:0] counter_1_q;

  Comparator #(.width(16), .mode("unsigned")) comparator_1 (
    .a(instruction), .b({16{1'b0}}), .eq(comparator_1_eq));  // open: gt, lt
  Counter #(.width(12), .max('hfff), .trigger("falling")) counter_1 (
    .Q(counter_1_q), .carry(counter_1_carry), .clk(clock), .clr(reset));  // open: load, D, count
  or or_1 (or_1_out, comparator_1_eq, counter_1_carry);
  Comparator #(.width(12), .mode("unsigned")) comparator_2 (
    .a(counter_1_q), .b({12{1'b0}}), .gt(comparator_2_gt));  // open: eq, lt
  or or_2 (or_2_out, halt, and_1_out);
  and and_1 (and_1_out, or_1_out, comparator_2_gt);
  Register #(.width(1)) register_1 (.D(or_2_out), .Q(halt), .clk(clock), .clr(reset));  // open: en

  // Notes on the sheet:
  //   halt becomes and stays asserted if the instruction is 0000 (not in the first clock cycle) or the end of the counter is reached (2^12)
endmodule

// PC
module _12BitProgramCounter (
  input  Branch_relative,
  input  Branch_absolute,
  input  [11:0] Branch_value,
  input  C,
  input  reset,
  output [11:0] Instruction_Address
);

  wire [11:0] multiplexer_1_out, multiplexer_2_out, n12bcla_1_out_4;

  Multiplexer #(.width(12), .enable("false")) multiplexer_1 (
    .in0({12{1'b0}}), .in1(Branch_value), .out(multiplexer_1_out), .sel(Branch_relative));
  _12bCLA u_12bcla_1 (
    .C_0(1'b1), .a(Instruction_Address), .b(multiplexer_1_out), .out_4(n12bcla_1_out_4));  // open: Overflow
  Multiplexer #(.width(12), .enable("false")) multiplexer_2 (
    .in0(n12bcla_1_out_4), .in1(Branch_value), .out(multiplexer_2_out), .sel(Branch_absolute));
  register register_1 (.D(multiplexer_2_out), .Q(Instruction_Address), .reset(reset), .write(1'b1), .C(C));
endmodule

module Decoder (
  input  [15:0] Instruction,
  output [2:0] Operation_Code,
  output [2:0] rd,
  output [2:0] rs,
  output [2:0] rt,
  output [3:0] Operational_Function_Code,
  output [11:0] Immediate_extended_9_bits,
  output [11:0] Immediate_extended_6_bits
);

  assign Immediate_extended_9_bits = {{3{Instruction[9]}}, Instruction[9:1]};  // Bit_Extender bit_extender_1
  assign Immediate_extended_6_bits = {{6{Instruction[6]}}, Instruction[6:1]};  // Bit_Extender bit_extender_2

  assign Operation_Code = Instruction[15:13];
  assign Operational_Function_Code = Instruction[3:0];
  assign rd = Instruction[12:10];
  assign rs = Instruction[9:7];
  assign rt = Instruction[6:4];
endmodule

// controller
module Controller (
  input  [3:0] Operational_Function_Code,
  input  [2:0] Operation_code,
  output Read_Memory,
  output Write_Memory,
  output SUBI,
  output [3:0] ALU_Operation,
  output Register_Write,
  output Load_Immediate_register,
  output Zero_Operation,
  output ALU_Immediate,
  output Use_Upper
);

  wire LDI_out, or_1_out, or_3_out;
  wire [1:0] multiplexer_1_out, Unary_out;
  wire [3:0] multiplexer_2_out;
  wire [3:3] not_1_out;

  not not_1 (not_1_out[3], Operational_Function_Code[3]);
  and r_mem (Read_Memory, Operation_code[2], Operation_code[1], Operation_code[0], ~Operational_Function_Code[0]);  // AND_Gate
  and w_mem (Write_Memory, Operation_code[2], Operation_code[1], Operation_code[0], Operational_Function_Code[0]);
  and u_subi (SUBI, Operation_code[2], ~Operation_code[1], ~Operation_code[0], Operational_Function_Code[0]);  // AND_Gate
  and Unary (Unary_out[0], ~Operation_code[2], ~Operation_code[1], Operation_code[0], ~Operational_Function_Code[3]);  // AND_Gate
  and Binary (Unary_out[1], ~Operation_code[2], Operation_code[1], ~Operation_code[0], ~Operational_Function_Code[3]);  // AND_Gate
  nor Zero (Zero_Operation, Operational_Function_Code[0], Operational_Function_Code[1], Operational_Function_Code[2], Operational_Function_Code[3], Operation_code[0], Operation_code[1], Operation_code[2]);
  and ALU_imm (ALU_Immediate, Operation_code[2], ~Operation_code[1], ~Operation_code[0]);  // AND_Gate
  and LDI (LDI_out, ~Operation_code[2], Operation_code[1], Operation_code[0], ~Operational_Function_Code[0]);  // AND_Gate
  and LUI (Use_Upper, ~Operation_code[2], Operation_code[1], Operation_code[0], Operational_Function_Code[0]);  // AND_Gate
  Multiplexer #(.width(2), .enable("false")) multiplexer_1 (
    .in0(Unary_out), .in1(2'b11), .out(multiplexer_1_out), .sel(Zero_Operation));
  or or_1 (or_1_out, Unary_out[1], Unary_out[0], ALU_Immediate, Zero_Operation);
  or or_2 (Load_Immediate_register, LDI_out, Use_Upper);
  or or_3 (or_3_out, Read_Memory, or_1_out);
  Multiplexer #(.select(2), .width(4), .enable("false")) multiplexer_2 (
    .in0(4'b0000), .in1(Operational_Function_Code), .in2({not_1_out[3], Operational_Function_Code[2:0]}),
    .in3(4'b1110), .out(multiplexer_2_out), .sel(multiplexer_1_out));
  or or_4 (Register_Write, or_3_out, Load_Immediate_register);
  Multiplexer #(.width(4), .enable("false")) multiplexer_3 (
    .in0(multiplexer_2_out), .in1({3'b000, Operational_Function_Code[0]}), .out(ALU_Operation),
    .sel(ALU_Immediate));
endmodule

// Swap
module swap (
  input  Switch,
  input  [11:0] Input_1,
  input  [11:0] Input_2,
  output [11:0] Output_1,
  output [11:0] Output_2
);

  Multiplexer #(.width(12), .enable("false")) multiplexer_1 (
    .in0(Input_1), .in1(Input_2), .out(Output_1), .sel(Switch));
  Multiplexer #(.width(12), .enable("false")) multiplexer_2 (
    .in0(Input_2), .in1(Input_1), .out(Output_2), .sel(Switch));
endmodule
