// Logisim project FDE_Group10.circ as structural Verilog: 7 circuits, main circuit main
module main (
  output [11:0] pc,
  output [11:0] r0,
  output [11:0] r1,
  output [11:0] r2,
  output [11:0] r3,
  output [11:0] r4,
  output [11:0] r5,
  output [11:0] r6,
  output [11:0] r7,
  output halt
);

  wire and_1_out, and_2_out, clock_1_out, controller_1_alu_immediate, controller_1_branch_absolute__j_jal_jr,
       controller_1_branch_relative__brnz, controller_1_jump_register__jr,
       controller_1_load_immediate_register, controller_1_rd_rs, controller_1_read_memory,
       controller_1_register_write, controller_1_return_address__jal, controller_1_subi,
       controller_1_use_upper, controller_1_write_memory, halt_1_halt,
       invalid_instruction_detector_1_alu_code_contains_nonsensical_function_code,
       invalid_instruction_detector_1_unary_alu_operation_contains_nonsensical_second_register,
       invalid_instruction_detector_1_zero_instruction_does_not_contain_0_immediate, n12_bit_alu_1_overflow,
       not_1_out, or_1_out, or_3_out, reset_out;
  wire [2:0] decoder_1_operation_code, decoder_1_rd, decoder_1_rs, decoder_1_rt, multiplexer_6_out,
       multiplexer_8_out;
  wire [3:0] controller_1_alu_operation, decoder_1_operational_function_code;
  wire [11:0] decoder_1_immediate_12_bits, decoder_1_immediate_extended_6_bits,
       decoder_1_immediate_extended_9_bits, multiplexer_1_out, multiplexer_2_out, multiplexer_3_out,
       multiplexer_4_out, multiplexer_5_out, multiplexer_7_out, multiplexer_9_out, multiplexer_10_out,
       n12_bit_alu_1_result, n12bcla_1_out_4, ram_2_data, registerfile_1_s, registerfile_1_t, shifter_1_out,
       swap_1_output_1, swap_1_output_2;
  wire [15:0] ram_1_data;

  and and_1 (and_1_out, n12_bit_alu_1_result[0], controller_1_branch_relative__brnz);
  Invalid_Instruction_Detector invalid_instruction_detector_1 (
    .Instruction(ram_1_data),
    .Zero_Instruction_does_not_contain_0_immediate(invalid_instruction_detector_1_zero_instruction_does_not_contain_0_immediate),
    .ALU_code_contains_nonsensical_function_code(invalid_instruction_detector_1_alu_code_contains_nonsensical_function_code),
    .Unary_ALU_operation_contains_nonsensical_second_register(invalid_instruction_detector_1_unary_alu_operation_contains_nonsensical_second_register));
  or or_1 (or_1_out, invalid_instruction_detector_1_zero_instruction_does_not_contain_0_immediate, invalid_instruction_detector_1_alu_code_contains_nonsensical_function_code, invalid_instruction_detector_1_unary_alu_operation_contains_nonsensical_second_register);
  Halt halt_1 (.instruction(ram_1_data), .clock(clock_1_out), .reset(reset_out), .halt(halt_1_halt));
  Clock clock_1 (.out(clock_1_out));
  Button reset (.out(reset_out));
  _12BitProgramCounter u_12bitprogramcounter_1 (
    .Branch_relative(and_1_out), .Branch_absolute(controller_1_branch_absolute__j_jal_jr),
    .Branch_value(multiplexer_1_out), .C(and_2_out), .reset(reset_out), .Instruction_Address(pc));
  _12bCLA u_12bcla_1 (.C_0(1'b1), .a({12{1'b0}}), .b(pc), .out_4(n12bcla_1_out_4));  // open: Overflow
  RAM #(.addrWidth(12), .dataWidth(16), .bus("asynch")) ram_1 (.addr(pc), .data(ram_1_data));  // open: sel, ld, clr
  Multiplexer #(.width(12), .enable("false")) multiplexer_1 (
    .in0(multiplexer_2_out), .in1(multiplexer_3_out), .out(multiplexer_1_out),
    .sel(controller_1_branch_relative__brnz));
  or or_2 (halt, halt_1_halt, or_1_out, n12_bit_alu_1_overflow);
  and and_2 (and_2_out, ~halt, clock_1_out);  // AND_Gate
  Decoder decoder_1 (
    .Instruction(ram_1_data), .Immediate_12_bits(decoder_1_immediate_12_bits),
    .Operation_Code(decoder_1_operation_code), .rd(decoder_1_rd), .rs(decoder_1_rs), .rt(decoder_1_rt),
    .Operational_Function_Code(decoder_1_operational_function_code),
    .Immediate_extended_9_bits(decoder_1_immediate_extended_9_bits),
    .Immediate_extended_6_bits(decoder_1_immediate_extended_6_bits));
  Multiplexer #(.width(12), .enable("false")) multiplexer_2 (
    .in0(decoder_1_immediate_12_bits), .in1(n12_bit_alu_1_result), .out(multiplexer_2_out),
    .sel(controller_1_jump_register__jr));
  Shifter #(.width(12)) shifter_1 (.in(decoder_1_immediate_extended_9_bits), .\dist (4'b0011), .out(shifter_1_out));
  Multiplexer #(.width(12), .enable("false")) multiplexer_3 (
    .in0(decoder_1_immediate_extended_9_bits), .in1(shifter_1_out), .out(multiplexer_3_out),
    .sel(controller_1_use_upper));
  not not_1 (not_1_out, controller_1_load_immediate_register);
  Multiplexer #(.width(12), .enable("false")) multiplexer_4 (
    .in0(multiplexer_3_out), .in1(multiplexer_5_out), .out(multiplexer_4_out), .sel(not_1_out));
  Multiplexer #(.width(12), .enable("false")) multiplexer_5 (
    .in0(n12_bit_alu_1_result), .in1(n12bcla_1_out_4), .out(multiplexer_5_out),
    .sel(controller_1_return_address__jal));
  Controller controller_1 (
    .Branch_Absolute__j_jal_jr(controller_1_branch_absolute__j_jal_jr),
    .Return_Address__jal(controller_1_return_address__jal),
    .Branch_Relative__brnz(controller_1_branch_relative__brnz),
    .Jump_Register__jr(controller_1_jump_register__jr), .Operation_code(decoder_1_operation_code),
    .Operational_Function_Code(decoder_1_operational_function_code), .Read_Memory(controller_1_read_memory),
    .Write_Memory(controller_1_write_memory), .SUBI(controller_1_subi),
    .ALU_Operation(controller_1_alu_operation), .Register_Write(controller_1_register_write),
    .Load_Immediate_register(controller_1_load_immediate_register), .rd_rs(controller_1_rd_rs),
    .ALU_Immediate(controller_1_alu_immediate), .Use_Upper(controller_1_use_upper));
  Multiplexer #(.width(3), .enable("false")) multiplexer_6 (
    .in0(decoder_1_rd), .in1(3'b111), .out(multiplexer_6_out), .sel(controller_1_return_address__jal));
  Multiplexer #(.width(12), .enable("false")) multiplexer_7 (
    .in0(multiplexer_4_out), .in1(ram_2_data), .out(multiplexer_7_out), .sel(controller_1_read_memory));
  Multiplexer #(.width(3), .enable("false")) multiplexer_8 (
    .in0(decoder_1_rt), .in1(decoder_1_rd), .out(multiplexer_8_out), .sel(controller_1_rd_rs));
  registerfile registerfile_1 (
    .C(and_2_out), .reset(reset_out), .rd(multiplexer_6_out), .Data(multiplexer_7_out),
    .write(controller_1_register_write), .rs(decoder_1_rs), .rt(multiplexer_8_out), .r0(r0), .r1(r1),
    .r2(r2), .r3(r3), .r4(r4), .r5(r5), .r6(r6), .r7(r7), .S(registerfile_1_s), .T(registerfile_1_t));
  Multiplexer #(.width(12), .enable("false")) multiplexer_9 (
    .in0(registerfile_1_s), .in1(multiplexer_3_out), .out(multiplexer_9_out), .sel(controller_1_alu_immediate));
  or or_3 (or_3_out, controller_1_write_memory, controller_1_read_memory);
  _12_bit_ALU u_12_bit_alu_1 (
    .ALU_code(controller_1_alu_operation), .a(swap_1_output_1), .b(swap_1_output_2),
    .overflow(n12_bit_alu_1_overflow), .result(n12_bit_alu_1_result));
  swap swap_1 (
    .Input_1(multiplexer_9_out), .Input_2(multiplexer_10_out), .Output_1(swap_1_output_1),
    .Output_2(swap_1_output_2), .Switch(controller_1_subi), .make_it_0(controller_1_branch_relative__brnz));
  Multiplexer #(.width(12), .enable("false")) multiplexer_10 (
    .in0(registerfile_1_t), .in1(decoder_1_immediate_extended_6_bits), .out(multiplexer_10_out),
    .sel(or_3_out));
  RAM #(.addrWidth(12), .dataWidth(12), .bus("separate")) ram_2 (
    .addr(n12_bit_alu_1_result), .din(registerfile_1_t), .data(ram_2_data), .str(controller_1_write_memory),
    .clk(and_2_out), .ld(controller_1_read_memory));  // open: sel, clr

  // Notes on the sheet:
  //   Instruction RAM
  //   current instruction
  //   clock signal
  //   reset
  //   reset button
  //   ALU exception
  //   DO NOT CHANGE THE INPUTS AND OUTPUTS OF THIS CIRCUIT! Do not add/remove inputs or outputs. Do not even change their location or orientation.
  //   Data RAM
endmodule

module Halt (
  input  [15:0] instruction,
  input  clock,
  input  reset,
  output halt
);

  wire and_1_out, comparator_1_eq, comparator_2_gt, counter_1_carry, or_1_out, or_2_out;
  wire [11:0] counter_1_q;

  Comparator #(.width(16), .mode("unsigned")) comparator_1 (
    .a(instruction), .b({16{1'b0}}), .eq(comparator_1_eq));  // open: gt, lt
  Counter #(.width(12), .max('hfff), .trigger("falling")) counter_1 (
    .Q(counter_1_q), .carry(counter_1_carry), .clk(clock), .clr(reset));  // open: load, D, count
  or or_1 (or_1_out, comparator_1_eq, counter_1_carry);
  Comparator #(.width(12), .mode("unsigned")) comparator_2 (
    .a(counter_1_q), .b({12{1'b0}}), .gt(comparator_2_gt));  // open: eq, lt
  or or_2 (or_2_out, halt, and_1_out);
  and and_1 (and_1_out, or_1_out, comparator_2_gt);
  Register #(.width(1)) register_1 (.D(or_2_out), .Q(halt), .clk(clock), .clr(reset));  // open: en

  // Notes on the sheet:
  //   halt becomes and stays asserted if the instruction is 0000 (not in the first clock cycle) or the end of the counter is reached (2^12)
endmodule

// PC
module _12BitProgramCounter (
  input  Branch_relative,
  input  Branch_absolute,
  input  [11:0] Branch_value,
  input  C,
  input  reset,
  output [11:0] Instruction_Address
);

  wire [11:0] multiplexer_1_out, multiplexer_2_out, n12bcla_1_out_4;

  Multiplexer #(.width(12), .enable("false")) multiplexer_1 (
    .in0({12{1'b0}}), .in1(Branch_value), .out(multiplexer_1_out), .sel(Branch_relative));
  _12bCLA u_12bcla_1 (
    .C_0(1'b1), .a(Instruction_Address), .b(multiplexer_1_out), .out_4(n12bcla_1_out_4));  // open: Overflow
  Multiplexer #(.width(12), .enable("false")) multiplexer_2 (
    .in0(n12bcla_1_out_4), .in1(Branch_value), .out(multiplexer_2_out), .sel(Branch_absolute));
  register register_1 (.D(multiplexer_2_out), .Q(Instruction_Address), .reset(reset), .write(1'b1), .C(C));
endmodule

module Decoder (
  input  [15:0] Instruction,
  output [2:0] Operation_Code,
  output [2:0] rd,
  output [2:0] rs,
  output [2:0] rt,
  output [3:0] Operational_Function_Code,
  output [11:0] Immediate_extended_9_bits,
  output [11:0] Immediate_12_bits,
  output [11:0] Immediate_extended_6_bits
);

  assign Immediate_extended_9_bits = {{3{Instruction[9]}}, Instruction[9:1]};  // Bit_Extender bit_extender_1
  assign Immediate_extended_6_bits = {{6{Instruction[6]}}, Instruction[6:1]};  // Bit_Extender bit_extender_2

  assign Immediate_12_bits = Instruction[12:1];
  assign Operation_Code = Instruction[15:13];
  assign Operational_Function_Code = Instruction[3:0];
  assign rd = Instruction[12:10];
  assign rs = Instruction[9:7];
  assign rt = Instruction[6:4];
endmodule

// controller
module Controller (
  input  [3:0] Operational_Function_Code,
  input  [2:0] Operation_code,
  output Read_Memory,
  output Write_Memory,
  output SUBI,
  output Branch_Absolute__j_jal_jr,
  output Return_Address__jal,
  output [3:0] ALU_Operation,
  output Branch_Relative__brnz,
  output Register_Write,
  output Load_Immediate_register,
  output rd_rs,
  output ALU_Immediate,
  output Jump_Register__jr,
  output Use_Upper
);

  wire ALU_imm_out, and_2_out, LDI_out, or_3_out, or_5_out, Zero_out;
  wire [1:0] multiplexer_1_out, Unary_out;
  wire [3:0] multiplexer_2_out, multiplexer_3_out;
  wire [3:3] not_1_out;

  or or_1 (Branch_Absolute__j_jal_jr, and_2_out, Jump_Register__jr);
  and and_1 (Return_Address__jal, and_2_out, Operational_Function_Code[0]);
  and and_2 (and_2_out, Operation_code[2], Operation_code[1], ~Operation_code[0]);  // AND_Gate
  and and_3 (Branch_Relative__brnz, Operation_code[2], ~Operation_code[1], Operation_code[0], ~Operational_Function_Code[0]);  // AND_Gate
  and and_4 (Jump_Register__jr, Operation_code[2], ~Operation_code[1], Operation_code[0], Operational_Function_Code[0]);  // AND_Gate
  not not_1 (not_1_out[3], Operational_Function_Code[3]);
  and ALU_imm (ALU_imm_out, Operation_code[2], ~Operation_code[1], ~Operation_code[0]);  // AND_Gate
  and r_mem (Read_Memory, Operation_code[2], Operation_code[1], Operation_code[0], ~Operational_Function_Code[0]);  // AND_Gate
  and w_mem (Write_Memory, Operation_code[2], Operation_code[1], Operation_code[0], Operational_Function_Code[0]);
  and u_subi (SUBI, Operation_code[2], ~Operation_code[1], ~Operation_code[0], Operational_Function_Code[0]);  // AND_Gate
  and Unary (Unary_out[0], ~Operation_code[2], ~Operation_code[1], Operation_code[0], ~Operational_Function_Code[3]);  // AND_Gate
  and Binary (Unary_out[1], ~Operation_code[2], Operation_code[1], ~Operation_code[0], ~Operational_Function_Code[3]);  // AND_Gate
  nor Zero (Zero_out, Operational_Function_Code[0], Operational_Function_Code[1], Operational_Function_Code[2], Operational_Function_Code[3], Operation_code[0], Operation_code[1], Operation_code[2]);
  and LDI (LDI_out, ~Operation_code[2], Operation_code[1], Operation_code[0], ~Operational_Function_Code[0]);  // AND_Gate
  and LUI (Use_Upper, ~Operation_code[2], Operation_code[1], Operation_code[0], Operational_Function_Code[0]);  // AND_Gate
  Multiplexer #(.width(2), .enable("false")) multiplexer_1 (
    .in0(Unary_out), .in1(2'b11), .out(multiplexer_1_out), .sel(Zero_out));
  or or_2 (ALU_Immediate, Jump_Register__jr, ALU_imm_out);
  or or_3 (or_3_out, Unary_out[1], Unary_out[0], ALU_imm_out, Zero_out);
  Multiplexer #(.select(2), .width(4), .enable("false")) multiplexer_2 (
    .in0(4'b0000), .in1(Operational_Function_Code), .in2({not_1_out[3], Operational_Function_Code[2:0]}),
    .in3(4'b1110), .out(multiplexer_2_out), .sel(multiplexer_1_out));
  or or_4 (Load_Immediate_register, LDI_out, Use_Upper);
  or or_5 (or_5_out, Read_Memory, or_3_out);
  or or_6 (Register_Write, or_5_out, Return_Address__jal, Load_Immediate_register);
  Multiplexer #(.width(4), .enable("false")) multiplexer_3 (
    .in0(multiplexer_2_out), .in1({3'b000, Operational_Function_Code[0]}), .out(multiplexer_3_out),
    .sel(ALU_imm_out));
  Multiplexer #(.width(4), .enable("false")) multiplexer_4 (
    .in0(multiplexer_3_out), .in1(4'b0111), .out(ALU_Operation), .sel(Branch_Relative__brnz));
  or or_7 (rd_rs, Read_Memory, Write_Memory, ALU_Immediate, Branch_Relative__brnz);

  // Other names for the same wires on the sheet: brnz = Branch_Relative__brnz
endmodule

// Swap
module swap (
  input  Switch,
  input  make_it_0,
  input  [11:0] Input_1,
  input  [11:0] Input_2,
  output [11:0] Output_1,
  output [11:0] Output_2
);

  wire [11:0] multiplexer_1_out;

  Multiplexer #(.width(12), .enable("false")) multiplexer_1 (
    .in0(Input_1), .in1(Input_2), .out(multiplexer_1_out), .sel(Switch));
  Multiplexer #(.width(12), .enable("false")) multiplexer_2 (
    .in0(Input_2), .in1(Input_1), .out(Output_2), .sel(Switch));
  Multiplexer #(.width(12), .enable("false")) multiplexer_3 (
    .in0(multiplexer_1_out), .in1({12{1'b0}}), .out(Output_1), .sel(make_it_0));
endmodule

// IID
module Invalid_Instruction_Detector (
  input  [15:0] Instruction,
  output Zero_Instruction_does_not_contain_0_immediate,
  output ALU_code_contains_nonsensical_function_code,
  output Unary_ALU_operation_contains_nonsensical_second_register
);

  wire and_3_out, and_4_out, and_6_out, and_7_out, or_1_out, or_2_out;

  and and_1 (Zero_Instruction_does_not_contain_0_immediate, and_7_out, or_1_out);
  and and_2 (ALU_code_contains_nonsensical_function_code, or_2_out, Instruction[3]);
  or or_1 (or_1_out, Instruction[9], Instruction[8], Instruction[7], Instruction[6], Instruction[5], Instruction[4], Instruction[3], Instruction[2], Instruction[1], Instruction[0]);
  and and_3 (and_3_out, ~Instruction[15], ~Instruction[14], Instruction[13]);  // AND_Gate
  or or_2 (or_2_out, and_3_out, and_4_out);
  and and_4 (and_4_out, ~Instruction[15], Instruction[14], ~Instruction[13]);  // AND_Gate
  and and_5 (Unary_ALU_operation_contains_nonsensical_second_register, and_4_out, and_6_out);
  and and_6 (and_6_out, Instruction[6], Instruction[5], Instruction[4]);
  and and_7 (and_7_out, ~Instruction[15], ~Instruction[14], ~Instruction[13]);  // AND_Gate

  // Notes on the sheet:
  //   Opcode
  //   rt
  //   rd
  //   rs
  //   function
endmodule
